# Fritzing sketch raspi-network-toggle (saved by Fritzing 0.9.3b)

parts:
  Raspberry_Pi_1 = Raspberry Pi 3 [part_number=RPI-3-V1.2]
  OMRON1 = OMRON PCB Power Relay – G5LE [part_number="G5LE-1\n" package=THT]
  U1 = mystery part, 2 pins [chip_label=Route]

nets:
  N1: Raspberry_Pi_1.GPIO26, OMRON1.COIL1
  N2: Raspberry_Pi_1.GND, OMRON1.COIL2
  N3: OMRON1.A, U1.pin1
  N4: OMRON1.C, U1.pin2
